// Logisim project 16to4E.circ as structural Verilog: 1 circuit, main circuit main
module main (
  input  _0,
  input  _1,
  input  _2,
  input  _3,
  input  _4,
  input  _5,
  input  _6,
  input  _7,
  input  _8,
  input  _9,
  input  _10,
  input  _11,
  input  _12,
  input  _13,
  input  _14,
  input  _15,
  output A0,
  output A1,
  output A2,
  output A3
);

  or or_1 (A0, _8, _9, _10, _11, _12, _13, _14, _15);
  or or_2 (A1, _4, _5, _6, _7, _12, _13, _14, _15);
  or or_3 (A2, _2, _3, _6, _7, _10, _11, _14, _15);
  or or_4 (A3, _1, _3, _5, _7, _9, _11, _13, _15);
endmodule
