// Logisim project 1bit_ALU.circ as structural Verilog: 1 circuit, main circuit main
module main (
  input  C,
  input  F0,
  input  F1,
  input  F2,
  input  B,
  input  A,
  input  constant_0,
  input  Constant_1,
  output Y0,
  output Y1
);

  wire multiplexer_1_out, multiplexer_2_out, multiplexer_3_out, multiplexer_5_out, xor_1_out, xor_2_out;

  xor xor_1 (xor_1_out, A, B);
  Multiplexer #(.enable("false")) multiplexer_1 (.in0(constant_0), .in1(B), .out(multiplexer_1_out), .sel(A));
  xor xor_2 (xor_2_out, C, xor_1_out);
  Multiplexer #(.enable("false")) multiplexer_2 (.in0(B), .in1(constant_0), .out(multiplexer_2_out), .sel(A));
  Multiplexer #(.enable("false")) multiplexer_3 (.in0(B), .in1(Constant_1), .out(multiplexer_3_out), .sel(A));
  Multiplexer #(.select(3)) multiplexer_4 (
    .in0(constant_0), .in1(multiplexer_3_out), .in2(multiplexer_1_out), .in3(xor_1_out), .in4(xor_1_out),
    .in5(xor_1_out), .in6(xor_2_out), .in7(xor_2_out), .out(Y0), .sel({F2, F1, F0}), .en(Constant_1));
  Multiplexer #(.enable("false")) multiplexer_5 (.in0(Constant_1), .in1(B), .out(multiplexer_5_out), .sel(A));
  Multiplexer #(.select(3)) multiplexer_6 (
    .in0(multiplexer_1_out), .in1(multiplexer_1_out), .in2(multiplexer_2_out), .in3(multiplexer_2_out),
    .in4(multiplexer_1_out), .in5(multiplexer_3_out), .in6(multiplexer_2_out), .in7(multiplexer_5_out),
    .out(Y1), .sel({F1, F0, C}), .en(F2));

  // Notes on the sheet:
  //   AB
  //   A'B
  //   A+B
  //   A'+B
endmodule
