// Logisim project 2nd.circ as structural Verilog: 1 circuit, main circuit main
module main (
  input  C,
  input  B,
  input  A,
  input  C_2,
  input  B_2,
  input  A_2,
  input  D,
  input  C_3,
  input  B_3,
  input  A_3,
  input  A_4,
  input  B_4,
  input  C_4,
  input  D_2,
  input  C_5,
  input  B_5,
  input  A_5,
  output out_18,
  output out_19,
  output out_20,
  output out_21,
  output out_22
);

  wire A_C_out, A_prime_2_out, A_prime_B_out, A_prime_C_2_out, A_prime_C_out, A_prime_out, AB_out,
       AB_prime_C_out, ABD_prime_out, AC_2_out, AC_out, and_3_out, and_4_out, B_A_C_out, B_C_out,
       B_prime_2_out, B_prime_C_out, B_prime_out, BC_B_C_out, BC_out, BD_prime_out, C_prime_D_out,
       C_prime_out, D_prime_out, not_1_out, or_1_out, or_2_out, or_4_out, or_5_out;

  not D_prime (D_prime_out, D_2);
  not C_prime (C_prime_out, C_3);
  not not_1 (not_1_out, A_4);
  or B_C (B_C_out, B, C);
  and BC (BC_out, B, C);
  and C_prime_D (C_prime_D_out, C_prime_out, D);
  not B_prime (B_prime_out, B_5);
  and AB (AB_out, A, B);
  and AC (AC_out, A_2, C_2);
  or A_C (A_C_out, A_2, C_2);
  and A_prime_C (A_prime_C_out, not_1_out, C_4);
  and A_prime_B (A_prime_B_out, not_1_out, B_4);
  and BC_B_C (BC_B_C_out, B_C_out, BC_out);
  not B_prime_2 (B_prime_2_out, B_3);
  not A_prime (A_prime_out, A_5);
  and B_A_C (B_A_C_out, B_2, A_C_out);
  and B_prime_C (B_prime_C_out, B_prime_2_out, C_3);
  or or_1 (or_1_out, A_prime_C_out, C_4);
  or or_2 (or_2_out, A_prime_B_out, C_4);
  and and_1 (out_18, AB_out, BC_B_C_out);
  or or_3 (out_19, A_2, AC_out, B_A_C_out);
  or or_4 (or_4_out, B_prime_C_out, C_prime_D_out);
  and and_2 (out_21, or_1_out, or_2_out);
  and A_prime_C_2 (A_prime_C_2_out, C_5, A_prime_out);
  and BD_prime (BD_prime_out, B_5, D_prime_out);
  and AB_prime_C (AB_prime_C_out, A_5, B_prime_out, C_5);
  and ABD_prime (ABD_prime_out, A_5, B_5, D_prime_out);
  not A_prime_2 (A_prime_2_out, A_3);
  and AC_2 (AC_2_out, A_5, C_5);
  and and_3 (and_3_out, B_3, or_4_out);
  or or_5 (or_5_out, B_5, AC_2_out);
  or or_6 (out_20, A_prime_2_out, and_3_out);
  and and_4 (and_4_out, or_5_out, A_prime_C_2_out);
  or or_7 (out_22, and_4_out, BD_prime_out, AB_prime_C_out, ABD_prime_out, B_5);

  // Notes on the sheet:
  //   !st EXAMPLE
  //   2nd EXAMPLE
  //   4th Example
  //   5th Example
  //   3rd EXAMPLE
  //   A'B+C
  //   A'C+B
  //   AB + BC(B+C)
  //   A+AC+B(A+C)
  //   B'C+C'D
  //   (A'C+B)(A'B+C)
  //   B(B'C+C'D)
  //   AC+B
  //   A'C(AC+B)
  //   A' + B(B'C + C'D)
  //   AB'C + B + BD' + ABD' + A'C(AC+B)
endmodule
