// Logisim project 3rd.circ as structural Verilog: 1 circuit, main circuit main
module main (
  input  A,
  input  B,
  input  C,
  input  A_2,
  input  B_2,
  input  C_2,
  input  D,
  input  A_3,
  input  B_3,
  input  C_3,
  input  D_2,
  output AB___BC___AC,
  output out_13,
  output out_14
);

  wire AB_2_out, AB_3_out, AB_out, AC_out, and_1_out, and_2_out, B_C_out, BC_out, CD_out, D_nC_out, nB_C_out,
       not_1_out, not_2_out, not_3_out, or_2_out, or_3_out, or_5_out, or_out;

  not not_1 (not_1_out, B_2);
  not not_2 (not_2_out, C_3);
  and AB (AB_out, A, B);
  and BC (BC_out, B, C);
  and AC (AC_out, C, A);
  or B_C (B_C_out, B_3, C_3);
  and D_nC (D_nC_out, not_2_out, D_2);
  and AB_2 (AB_2_out, A_3, B_3);
  or \or  (or_out, B_3, B_C_out);
  or or_2 (or_2_out, AB_out, BC_out);
  and AB_3 (AB_3_out, A_2, B_2);
  not not_3 (not_3_out, nB_C_out);
  or nB_C (nB_C_out, not_1_out, C_2);
  and CD (CD_out, C_2, D);
  and and_1 (and_1_out, AB_2_out, or_out);
  or or_3 (or_3_out, or_out, D_nC_out);
  or or_4 (AB___BC___AC, or_2_out, AC_out);
  and and_2 (and_2_out, AB_3_out, not_3_out);
  or or_5 (or_5_out, not_3_out, CD_out);
  and and_3 (out_13, and_2_out, or_5_out);
  and and_4 (out_14, and_1_out, or_3_out);

  // Notes on the sheet:
  //   B+(B+C)
  //   !st
  //   2nd
  //   3rd
  //   AB+BC
  //   (B+(B+C) + ~CD)
  //   AB~(~B+C)
  //   CD+(~B+C)
  //   AB~(~B+C) (CD + (~B+C))
  //   (AB(B+((B+C)))(B+(B+C)+~CD)
endmodule
