// Logisim project 4to2E.circ as structural Verilog: 1 circuit, main circuit main
module main (
  input  I0,
  input  I1,
  input  I2,
  input  I3,
  output A0,
  output A1
);

  or or_1 (A0, I2, I3);
  or or_2 (A1, I1, I3);
endmodule
