// Logisim project 4to2PE.circ as structural Verilog: 1 circuit, main circuit main
module main (
  input  I0,
  input  I1,
  input  I2,
  input  I3,
  output A1,
  output A0
);

  wire and_1_out, not_1_out;

  not not_1 (not_1_out, I2);
  and and_1 (and_1_out, not_1_out, I1);
  or or_1 (A1, and_1_out, I3);
  or or_2 (A0, I2, I3);
endmodule
