// Logisim project 7segment.circ as structural Verilog: 1 circuit, main circuit main
module main (
  input  A,
  input  B,
  input  C,
  input  D
);

  wire a_out, A_prime_out, b_out, B_prime_C_out, B_prime_D_prime_out, B_prime_out, BC_prime_D_out,
       BC_prime_out, BD_out, BD_prime_out, c_out, C_prime_D_prime_out, C_prime_out, CD_out, CD_prime_out,
       d_out, D_prime_out, e_out, f_out, g_out;

  not A_prime (A_prime_out, A);
  not B_prime (B_prime_out, B);
  not C_prime (C_prime_out, C);
  not D_prime (D_prime_out, D);
  and B_prime_D_prime (B_prime_D_prime_out, B_prime_out, D_prime_out);
  and BD (BD_out, B, D);
  and CD (CD_out, C, D);
  and C_prime_D_prime (C_prime_D_prime_out, C_prime_out, D_prime_out);
  and B_prime_C (B_prime_C_out, B_prime_out, C);
  and CD_prime (CD_prime_out, C, D_prime_out);
  and BC_prime_D (BC_prime_D_out, B, C_prime_out, D);
  and BD_prime (BD_prime_out, B, D_prime_out);
  and BC_prime (BC_prime_out, B, C_prime_out);
  or u_a (a_out, A, C, B_prime_D_prime_out, BD_out);
  or u_b (b_out, B_prime_out, CD_out, C_prime_D_prime_out);
  or u_c (c_out, C_prime_out, D, B);
  or u_d (d_out, A, B_prime_C_out, B_prime_D_prime_out, CD_prime_out, BC_prime_D_out);
  or e (e_out, B_prime_D_prime_out, CD_prime_out);
  or f (f_out, A, BC_prime_out, C_prime_D_prime_out, BD_prime_out);
  or g (g_out, A, BC_prime_out, CD_prime_out, B_prime_C_out);
  _7_Segment_Display u_7_segment_display_1 (
    .g(g_out), .f(f_out), .a(a_out), .b(b_out), .e(e_out), .d(d_out), .c(c_out));  // open: dp
endmodule
