// Logisim project 8to1M.circ as structural Verilog: 1 circuit, main circuit main
module main (
  input  I0,
  input  I1,
  input  I2,
  input  I3,
  input  I4,
  input  I5,
  input  I6,
  input  I7,
  input  S2,
  input  S1,
  input  S0,
  output Y
);

  wire _0_out, _1_out, _2_out, _3_out, _4_out, _5_out, _6_out, _7_out, not_1_out, not_2_out, not_3_out;

  not not_1 (not_1_out, S2);
  not not_2 (not_2_out, S1);
  not not_3 (not_3_out, S0);
  and _0 (_0_out, not_1_out, not_2_out, not_3_out, I0);
  and _1 (_1_out, not_1_out, not_2_out, S0, I1);
  and _2 (_2_out, not_1_out, S1, not_3_out, I2);
  and _3 (_3_out, not_1_out, S1, S0, I3);
  and _4 (_4_out, S2, not_2_out, not_3_out, I4);
  and _5 (_5_out, S2, not_2_out, S0, I5);
  and _6 (_6_out, S2, S1, not_3_out, I6);
  and _7 (_7_out, S2, S1, S0, I7);
  or or_1 (Y, _0_out, _1_out, _2_out, _3_out, _4_out, _5_out, _6_out, _7_out);
endmodule
