// Logisim project 8to3E.circ as structural Verilog: 1 circuit, main circuit main
module main (
  input  D1,
  input  D2,
  input  D3,
  input  D4,
  input  D5,
  input  D6,
  input  D7,
  output A0,
  output A1,
  output A2
);

  or or_1 (A0, D4, D5, D6, D7);
  or or_2 (A1, D2, D3, D6, D7);
  or or_3 (A2, D1, D3, D5, D7);
endmodule
