// Logisim project Examples.circ as structural Verilog: 1 circuit, main circuit main
module main (
  input  A,
  input  B,
  input  C,
  input  A_2,
  input  B_2,
  input  C_2,
  input  B_3,
  input  C_3,
  input  A_3,
  input  B_4,
  input  C_4,
  output out_12,
  output out_13,
  output out_14,
  output out_15
);

  wire and_1_out, and_2_out, and_3_out, B_prime_2_out, B_prime_out, not_1_out, or_2_out, xnor_1_out;

  not B_prime (B_prime_out, B_3);
  not B_prime_2 (B_prime_2_out, B_2);
  not not_1 (not_1_out, B_4);
  and and_1 (and_1_out, A, C);
  and and_2 (and_2_out, A_3, not_1_out, C_4);
  xnor xnor_1 (xnor_1_out, B_4, C_4);
  or or_1 (out_12, and_1_out, B);
  and and_3 (and_3_out, A_2, or_2_out);
  or or_2 (or_2_out, B_prime_2_out, C_2);
  and and_4 (out_14, B_prime_out, C_3);
  or or_3 (out_15, and_2_out, xnor_1_out);
  or or_4 (out_13, and_3_out, B_2);

  // Notes on the sheet:
  //   1st = B + AC
  //   2nd = A(B' + C) + B
  //   4th = B XNOR C + AB'C
  //   3rd = B'C
endmodule
