// Logisim project Flip-Flops.circ as structural Verilog: 1 circuit, main circuit main
module main (
  input  R,
  input  S,
  input  D,
  input  K,
  input  J,
  input  T,
  output out_7,
  output out_8,
  output out_9,
  output out_10,
  output out_11,
  output out_12,
  output out_13,
  output out_14
);

  wire and_1_out, and_2_out, and_3_out, and_4_out, and_5_out, and_6_out, and_7_out, and_8_out, clock_1_out,
       clock_2_out, clock_3_out, clock_4_out, not_1_out;

  Clock clock_1 (.out(clock_1_out));
  Clock clock_2 (.out(clock_2_out));
  Clock clock_3 (.out(clock_3_out));
  not not_1 (not_1_out, D);
  Clock clock_4 (.out(clock_4_out));
  and and_1 (and_1_out, R, clock_1_out);
  and and_2 (and_2_out, clock_1_out, S);
  and and_3 (and_3_out, not_1_out, clock_2_out);
  and and_4 (and_4_out, clock_2_out, D);
  and and_5 (and_5_out, out_11, K, clock_3_out);
  and and_6 (and_6_out, clock_3_out, J, out_12);
  and and_7 (and_7_out, out_13, T, clock_4_out);
  and and_8 (and_8_out, clock_4_out, T, out_14);
  nor nor_1 (out_7, and_1_out, out_8);
  nor nor_2 (out_8, out_7, and_2_out);
  nor nor_3 (out_9, and_3_out, out_10);
  nor nor_4 (out_10, out_9, and_4_out);
  nor nor_5 (out_11, and_5_out, out_12);
  nor nor_6 (out_12, out_11, and_6_out);
  nor nor_7 (out_13, and_7_out, out_14);
  nor nor_8 (out_14, out_13, and_8_out);

  // Notes on the sheet:
  //   SR Flip Flop
  //   D Flip Flop
  //   JK Flip Flop
  //   T Flip Flop
endmodule
