// Logisim project ModN.circ as structural Verilog: 1 circuit, main circuit main
module main (
  input  in_1,
  input  in_2
);

  wire and_1_out, and_2_out, clock_1_out, clock_2_out, j_k_ff_1_q, j_k_ff_1_qn, j_k_ff_2_q, j_k_ff_3_q,
       j_k_ff_4_q, j_k_ff_4_qn, j_k_ff_5_q, j_k_ff_6_q, not_1_out, not_2_out;

  Clock clock_1 (.out(clock_1_out));
  Clock clock_2 (.out(clock_2_out));
  LED led_1 (.in(j_k_ff_1_q));
  J_K_Flip_Flop j_k_ff_1 (
    .J(in_1), .clk(clock_1_out), .K(in_1), .Q(j_k_ff_1_q), .Qn(j_k_ff_1_qn), .preset(and_1_out));  // open: en, reset
  LED led_2 (.in(j_k_ff_2_q));
  J_K_Flip_Flop j_k_ff_2 (
    .J(in_2), .clk(clock_2_out), .K(in_2), .Q(j_k_ff_2_q), .preset(and_2_out));  // open: Qn, en, reset
  LED led_3 (.in(j_k_ff_3_q));
  J_K_Flip_Flop j_k_ff_3 (
    .J(in_2), .clk(j_k_ff_2_q), .K(in_2), .Q(j_k_ff_3_q), .reset(and_2_out));  // open: Qn, preset, en
  LED led_4 (.in(j_k_ff_4_q));
  J_K_Flip_Flop j_k_ff_4 (
    .J(in_1), .clk(j_k_ff_1_qn), .K(in_1), .Q(j_k_ff_4_q), .Qn(j_k_ff_4_qn), .reset(and_1_out));  // open: preset, en
  and and_1 (and_1_out, j_k_ff_6_q, j_k_ff_4_q, j_k_ff_1_q);
  LED led_5 (.in(j_k_ff_5_q));
  J_K_Flip_Flop j_k_ff_5 (
    .J(in_2), .clk(j_k_ff_3_q), .K(in_2), .Q(j_k_ff_5_q), .preset(and_2_out));  // open: Qn, en, reset
  and and_2 (and_2_out, j_k_ff_2_q, not_1_out, not_2_out);
  LED led_6 (.in(j_k_ff_6_q));
  J_K_Flip_Flop j_k_ff_6 (
    .J(in_1), .clk(j_k_ff_4_qn), .K(in_1), .Q(j_k_ff_6_q), .reset(and_1_out));  // open: Qn, preset, en
  not not_1 (not_1_out, j_k_ff_3_q);
  not not_2 (not_2_out, j_k_ff_5_q);

  // Notes on the sheet:
  //   5-2 counter
  //   1-6 Counter
endmodule
