// Logisim project anushthan_saxena_exp01.circ as structural Verilog: 1 circuit, main circuit main
module main (
  input  A,
  input  A_2,
  input  A_3,
  input  B,
  input  A_4,
  input  B_2,
  input  B_3,
  input  A_5,
  input  B_4,
  output out_10,
  output out_11,
  output out_12,
  output out_13,
  output out_14
);

  wire _1_2_out, _1_3_out, _1_4_out, _1_out, _2_2_out, _2_4_out, _2_out, _3_2_out, _3_3_out;

  nand nand_1 (out_10, A, A);
  nand _1 (_1_out, A_2, B);
  nand _1_2 (_1_2_out, A_4, A_4);
  nand _2 (_2_out, B_3, B_3);
  nand _1_3 (_1_3_out, A_5, A_5);
  nand _2_2 (_2_2_out, B_4, B_4);
  nand _2_3 (out_11, _1_out, _1_out);
  nand _3 (out_13, _1_2_out, _2_out);
  nand _3_2 (_3_2_out, _1_3_out, _2_2_out);
  nand _4 (out_14, _3_2_out, _3_2_out);
  nand _1_4 (_1_4_out, A_3, B_2);
  nand _2_4 (_2_4_out, A_3, _1_4_out);
  nand _3_3 (_3_3_out, _1_4_out, B_2);
  nand _4_2 (out_12, _2_4_out, _3_3_out);

  // Notes on the sheet:
  //   Not gate
  //   And gate
  //   Or gate
  //   Nor gate
  //   Xor gate
endmodule
