// Logisim project counter_down.circ as structural Verilog: 1 circuit, main circuit main
module main (
);

  wire clock_1_out, clock_2_out, d_ff_1_q, d_ff_1_qn, d_ff_2_q, d_ff_2_qn, d_ff_3_q, d_ff_4_q, d_ff_4_qn,
       d_ff_5_q, d_ff_5_qn, d_ff_6_q, d_ff_7_q, d_ff_7_qn, d_ff_8_q, or_1_out, or_2_out, xnor_1_out,
       xnor_2_out, xnor_3_out;

  Clock clock_1 (.out(clock_1_out));
  D_Flip_Flop d_ff_1 (.clk(clock_1_out), .D(d_ff_1_qn), .Q(d_ff_1_q), .Qn(d_ff_1_qn));  // open: preset, en, reset
  Clock clock_2 (.out(clock_2_out));
  LED led_1 (.in(d_ff_1_q));
  D_Flip_Flop d_ff_2 (.clk(clock_2_out), .D(d_ff_2_qn), .Q(d_ff_2_q), .Qn(d_ff_2_qn));  // open: preset, en, reset
  xnor xnor_1 (xnor_1_out, d_ff_3_q, d_ff_1_q);
  LED led_2 (.in(d_ff_2_q));
  D_Flip_Flop d_ff_3 (.clk(clock_1_out), .D(xnor_1_out), .Q(d_ff_3_q));  // open: Qn, preset, en, reset
  D_Flip_Flop d_ff_4 (.clk(d_ff_2_q), .D(d_ff_4_qn), .Q(d_ff_4_q), .Qn(d_ff_4_qn));  // open: preset, en, reset
  LED led_3 (.in(d_ff_3_q));
  or or_1 (or_1_out, d_ff_1_q, d_ff_3_q);
  LED led_4 (.in(d_ff_4_q));
  D_Flip_Flop d_ff_5 (.clk(d_ff_4_q), .D(d_ff_5_qn), .Q(d_ff_5_q), .Qn(d_ff_5_qn));  // open: preset, en, reset
  xnor xnor_2 (xnor_2_out, or_1_out, d_ff_6_q);
  D_Flip_Flop d_ff_6 (.clk(clock_1_out), .D(xnor_2_out), .Q(d_ff_6_q));  // open: Qn, preset, en, reset
  LED led_5 (.in(d_ff_5_q));
  LED led_6 (.in(d_ff_6_q));
  LED led_7 (.in(d_ff_7_q));
  D_Flip_Flop d_ff_7 (.clk(d_ff_5_q), .D(d_ff_7_qn), .Q(d_ff_7_q), .Qn(d_ff_7_qn));  // open: preset, en, reset
  or or_2 (or_2_out, d_ff_1_q, d_ff_3_q, d_ff_6_q);
  LED led_8 (.in(d_ff_8_q));
  xnor xnor_3 (xnor_3_out, or_2_out, d_ff_8_q);
  D_Flip_Flop d_ff_8 (.clk(clock_1_out), .D(xnor_3_out), .Q(d_ff_8_q));  // open: Qn, preset, en, reset

  // Notes on the sheet:
  //   Q0
  //   Q0
  //   asynchronous 4 bit down counter
  //   Q1
  //   Synchronous 4 bit down counter
  //   Q1
  //   Q2
  //   Q2
  //   Q3
  //   Q3
endmodule
