// Logisim project counter_up_synchronous.circ as structural Verilog: 1 circuit, main circuit main
module main (
);

  wire and_1_out, and_2_out, clock_1_out, d_ff_1_q, d_ff_1_qn, d_ff_2_q, d_ff_3_q, d_ff_4_q, xor_1_out,
       xor_2_out, xor_3_out;

  Clock clock_1 (.out(clock_1_out));
  D_Flip_Flop d_ff_1 (.clk(clock_1_out), .D(d_ff_1_qn), .Q(d_ff_1_q), .Qn(d_ff_1_qn));  // open: preset, en, reset
  LED led (.in(d_ff_1_q));
  xor xor_1 (xor_1_out, d_ff_2_q, d_ff_1_q);
  D_Flip_Flop d_ff_2 (.clk(clock_1_out), .D(xor_1_out), .Q(d_ff_2_q));  // open: Qn, preset, en, reset
  LED led_2 (.in(d_ff_2_q));
  and and_1 (and_1_out, d_ff_1_q, d_ff_2_q);
  xor xor_2 (xor_2_out, and_1_out, d_ff_3_q);
  LED led_3 (.in(d_ff_3_q));
  D_Flip_Flop d_ff_3 (.clk(clock_1_out), .D(xor_2_out), .Q(d_ff_3_q));  // open: Qn, preset, en, reset
  and and_2 (and_2_out, d_ff_1_q, d_ff_2_q, d_ff_3_q);
  LED led_4 (.in(d_ff_4_q));
  xor xor_3 (xor_3_out, and_2_out, d_ff_4_q);
  D_Flip_Flop d_ff_4 (.clk(clock_1_out), .D(xor_3_out), .Q(d_ff_4_q));  // open: Qn, preset, en, reset

  // Notes on the sheet:
  //   Q0
  //   Q1
  //   synchronous 4 bit up counter
  //   Q2
  //   Q3
endmodule
