// Logisim project 16to1M.circ as structural Verilog: 1 circuit, main circuit main
module main (
  input  S3,
  input  S2,
  input  S1,
  input  S0,
  input  I0,
  input  I1,
  input  I2,
  input  I3,
  input  I4,
  input  I5,
  input  I6,
  input  I7,
  input  I8,
  input  I9,
  input  I10,
  input  I11,
  input  I12,
  input  I13,
  input  I14,
  input  I15,
  output Y
);

  wire _0_out, _1_out, _2_out, _3_out, _4_out, _5_out, _6_out, _7_out, _8_out, _9_out, _10_out, _11_out,
       _12_out, _13_out, _14_out, _15_out, not_1_out, not_2_out, not_3_out, not_4_out;

  not not_1 (not_1_out, S3);
  not not_2 (not_2_out, S2);
  not not_3 (not_3_out, S1);
  not not_4 (not_4_out, S0);
  and _0 (_0_out, I0, not_1_out, not_2_out, not_3_out, not_4_out);
  and _1 (_1_out, I1, not_1_out, not_2_out, not_3_out, S0);
  and _2 (_2_out, I2, not_1_out, not_2_out, S1, not_4_out);
  and _3 (_3_out, I3, not_1_out, not_2_out, S1, S0);
  and _4 (_4_out, I4, not_1_out, S2, not_3_out, not_4_out);
  and _5 (_5_out, I5, not_1_out, S2, not_3_out, S0);
  and _6 (_6_out, I6, not_1_out, S2, S1, not_4_out);
  and _7 (_7_out, I7, not_1_out, S2, S1, S0);
  and _8 (_8_out, I8, S3, not_2_out, not_3_out, not_4_out);
  and _9 (_9_out, I9, S3, not_2_out, not_3_out, S0);
  and _10 (_10_out, I10, S3, not_2_out, S1, not_4_out);
  and _11 (_11_out, I11, S3, not_2_out, S1, S0);
  and _12 (_12_out, I12, S3, S2, not_3_out, not_4_out);
  and _13 (_13_out, I13, S3, S2, not_3_out, S0);
  and _14 (_14_out, I14, S3, S2, S1, not_4_out);
  and _15 (_15_out, I15, S3, S2, S1, S0);
  or or_1 (Y, _0_out, _1_out, _2_out, _3_out, _4_out, _5_out, _6_out, _7_out, _8_out, _9_out, _10_out, _11_out, _12_out, _13_out, _14_out, _15_out);
endmodule
