// Logisim project 2to4.circ as structural Verilog: 1 circuit, main circuit main
module main (
  input  A,
  input  B,
  input  E,
  output Y0,
  output Y1,
  output Y2,
  output Y3
);

  wire not_1_out, not_2_out;

  not not_1 (not_1_out, A);
  not not_2 (not_2_out, B);
  and and_1 (Y0, not_1_out, not_2_out, E);
  and and_2 (Y1, not_1_out, B, E);
  and and_3 (Y2, A, not_2_out, E);
  and and_4 (Y3, A, B, E);
endmodule
