// Logisim project 3to8and4to16.circ as structural Verilog: 2 circuits, main circuit main
module main (
  input  E,
  input  A,
  input  B,
  input  C,
  output Y0,
  output Y1,
  output Y2,
  output Y3,
  output Y4,
  output Y5,
  output Y6,
  output Y7
);

  wire not_1_out, not_2_out, not_3_out;

  not not_1 (not_1_out, A);
  not not_2 (not_2_out, B);
  not not_3 (not_3_out, C);
  and and_1 (Y0, not_1_out, not_2_out, not_3_out, E);
  and and_2 (Y1, not_1_out, not_2_out, C, E);
  and and_3 (Y2, not_1_out, B, not_3_out, E);
  and and_4 (Y3, not_1_out, B, C, E);
  and and_5 (Y4, A, not_2_out, not_3_out, E);
  and and_6 (Y5, A, not_2_out, C, E);
  and and_7 (Y6, A, B, not_3_out, E);
  and and_8 (Y7, A, B, C, E);
endmodule

module _4to16 (
  input  A,
  input  B,
  input  C,
  input  D,
  output Y0,
  output Y1,
  output Y2,
  output Y3,
  output Y4,
  output Y5,
  output Y6,
  output Y7,
  output Y8,
  output Y9,
  output Y10,
  output Y11,
  output Y12,
  output Y13,
  output Y14,
  output Y15
);

  wire not_1_out;

  not not_1 (not_1_out, A);
  main main_1 (
    .A(B), .B(C), .C(D), .E(not_1_out), .Y0(Y0), .Y1(Y1), .Y2(Y2), .Y3(Y3), .Y4(Y4), .Y5(Y5), .Y6(Y6), .Y7(Y7));
  main main_2 (
    .A(B), .B(C), .C(D), .E(A), .Y0(Y8), .Y1(Y9), .Y2(Y10), .Y3(Y11), .Y4(Y12), .Y5(Y13), .Y6(Y14), .Y7(Y15));
endmodule
