// Logisim project 8to3E.circ as structural Verilog: 1 circuit, main circuit main
module main (
  input  I1,
  input  I2,
  input  I3,
  input  I4,
  input  I5,
  input  I6,
  input  I7,
  output A0,
  output A1,
  output A2
);

  or or_1 (A0, I4, I5, I6, I7);
  or or_2 (A1, I2, I3, I6, I7);
  or or_3 (A2, I1, I3, I5, I7);
endmodule
