// Logisim project AdderSubtractor.circ as structural Verilog: 1 circuit, main circuit main
module main (
  input  A,
  input  B,
  input  A_2,
  input  B_2,
  input  C,
  input  A_3,
  input  B_3,
  input  A_4,
  input  B_4,
  input  C_2,
  output SUM,
  output CARRY,
  output SUM_2,
  output CARRY_2,
  output DIFFERENCE,
  output BORROW,
  output DIFFERENCE_2,
  output BORROW_2
);

  wire AB_2_out, and_2_out, and_3_out, and_4_out, not_1_out, not_2_out, not_3_out, xor_2_out, xor_4_out;

  not not_1 (not_1_out, A_3);
  not not_2 (not_2_out, A_4);
  xor xor_1 (SUM, A, B);
  and AB (CARRY, A, B);
  xor xor_2 (xor_2_out, A_2, B_2);
  xor xor_3 (DIFFERENCE, A_3, B_3);
  and and_1 (BORROW, not_1_out, B_3);
  xor xor_4 (xor_4_out, A_4, B_4);
  and and_2 (and_2_out, not_2_out, B_4);
  and and_3 (and_3_out, xor_2_out, C);
  and AB_2 (AB_2_out, A_2, B_2);
  not not_3 (not_3_out, xor_4_out);
  xor xor_5 (SUM_2, xor_2_out, C);
  or or_1 (CARRY_2, and_3_out, AB_2_out);
  xor xor_6 (DIFFERENCE_2, xor_4_out, C_2);
  and and_4 (and_4_out, not_3_out, C_2);
  or or_2 (BORROW_2, and_4_out, and_2_out);

  // Notes on the sheet:
  //   First Half Subtractor
  //   A XOR B
  //   A XOR B
  //   Half Adder
  //   C(A XOR B)
  //   A XOR B XOR C
  //   Half Subtractor
  //   Second Half Subtractor
  //   Full Adder
  //   Full Subtractor
endmodule
