// Logisim project Counter_JK_down.circ as structural Verilog: 1 circuit, main circuit main
module main (
  input  in_1,
  input  in_2
);

  wire and_1_out, and_2_out, clock_1_out, clock_2_out, j_k_ff_1_q, j_k_ff_2_q, j_k_ff_2_qn, j_k_ff_3_q,
       j_k_ff_3_qn, j_k_ff_4_q, j_k_ff_5_q, j_k_ff_6_q, j_k_ff_6_qn, j_k_ff_7_q, j_k_ff_8_q;

  Clock clock_1 (.out(clock_1_out));
  Clock clock_2 (.out(clock_2_out));
  J_K_Flip_Flop j_k_ff_1 (.J(in_2), .clk(clock_2_out), .K(in_2), .Q(j_k_ff_1_q));  // open: Qn, preset, en, reset
  LED led_1 (.in(j_k_ff_2_q));
  J_K_Flip_Flop j_k_ff_2 (
    .J(in_1), .clk(clock_1_out), .K(in_1), .Q(j_k_ff_2_q), .Qn(j_k_ff_2_qn));  // open: preset, en, reset
  LED led_2 (.in(j_k_ff_1_q));
  J_K_Flip_Flop j_k_ff_3 (
    .J(j_k_ff_2_qn), .clk(clock_1_out), .K(j_k_ff_2_qn), .Q(j_k_ff_3_q), .Qn(j_k_ff_3_qn));  // open: preset, en, reset
  LED led_3 (.in(j_k_ff_4_q));
  J_K_Flip_Flop j_k_ff_4 (.J(in_2), .clk(j_k_ff_1_q), .K(in_2), .Q(j_k_ff_4_q));  // open: Qn, preset, en, reset
  LED led_4 (.in(j_k_ff_3_q));
  and and_1 (and_1_out, j_k_ff_3_qn, j_k_ff_2_qn);
  J_K_Flip_Flop j_k_ff_5 (.J(in_2), .clk(j_k_ff_4_q), .K(in_2), .Q(j_k_ff_5_q));  // open: Qn, preset, en, reset
  LED led_5 (.in(j_k_ff_5_q));
  LED led_6 (.in(j_k_ff_6_q));
  J_K_Flip_Flop j_k_ff_6 (
    .J(and_1_out), .clk(clock_1_out), .K(and_1_out), .Q(j_k_ff_6_q), .Qn(j_k_ff_6_qn));  // open: preset, en, reset
  and and_2 (and_2_out, j_k_ff_6_qn, and_1_out);
  LED led_7 (.in(j_k_ff_7_q));
  J_K_Flip_Flop j_k_ff_7 (.J(in_2), .clk(j_k_ff_5_q), .K(in_2), .Q(j_k_ff_7_q));  // open: Qn, preset, en, reset
  LED led_8 (.in(j_k_ff_8_q));
  J_K_Flip_Flop j_k_ff_8 (
    .J(and_2_out), .clk(clock_1_out), .K(and_2_out), .Q(j_k_ff_8_q));  // open: Qn, preset, en, reset

  // Notes on the sheet:
  //   Asynchronous down counter
  //   Synchronous down counter
endmodule
