// Logisim project Direct_Flip_Flops.circ as structural Verilog: 1 circuit, main circuit main
module main (
  input  S,
  input  R,
  input  D,
  input  J,
  input  K,
  input  T,
  output out_7,
  output out_8,
  output out_9,
  output out_10,
  output out_11,
  output out_12,
  output out_13,
  output out_14
);

  wire clock_1_out, clock_2_out, clock_3_out, clock_4_out;

  Clock clock_1 (.out(clock_1_out));
  Clock clock_2 (.out(clock_2_out));
  Clock clock_3 (.out(clock_3_out));
  Clock clock_4 (.out(clock_4_out));
  S_R_Flip_Flop s_r_ff_1 (.S(S), .clk(clock_1_out), .R(R), .Q(out_7), .Qn(out_8));  // open: preset, reset, en
  D_Flip_Flop d_ff_1 (.clk(clock_2_out), .D(D), .Q(out_9), .Qn(out_10));  // open: preset, en, reset
  J_K_Flip_Flop j_k_ff_1 (.J(J), .clk(clock_3_out), .K(K), .Q(out_11), .Qn(out_12));  // open: preset, en, reset
  T_Flip_Flop t_ff_1 (.clk(clock_4_out), .T(T), .Q(out_13), .Qn(out_14));  // open: preset, reset, en
endmodule
