// Logisim project RIng_Johnson_Counter.circ as structural Verilog: 1 circuit, main circuit main
module main (
  input  in_1,
  input  in_2
);

  wire clock_1_out, clock_2_out, d_ff_1_q, d_ff_2_q, d_ff_3_q, d_ff_4_q, d_ff_5_q, d_ff_6_q, d_ff_7_q,
       d_ff_8_q, d_ff_9_q, d_ff_10_q, d_ff_10_qn;

  Clock clock_1 (.out(clock_1_out));
  Clock clock_2 (.out(clock_2_out));
  D_Flip_Flop #(.trigger("falling")) d_ff_1 (
    .clk(clock_1_out), .D(d_ff_9_q), .Q(d_ff_1_q), .preset(in_1));  // open: Qn, en, reset
  D_Flip_Flop #(.trigger("falling")) d_ff_2 (
    .clk(clock_2_out), .D(d_ff_10_qn), .Q(d_ff_2_q), .reset(in_2));  // open: Qn, preset, en
  LED led_1 (.in(d_ff_1_q));
  LED led_2 (.in(d_ff_2_q));
  LED led_3 (.in(d_ff_3_q));
  D_Flip_Flop #(.trigger("falling")) d_ff_3 (
    .clk(clock_1_out), .D(d_ff_1_q), .Q(d_ff_3_q), .reset(in_1));  // open: Qn, preset, en
  LED led_4 (.in(d_ff_4_q));
  D_Flip_Flop #(.trigger("falling")) d_ff_4 (
    .clk(clock_2_out), .D(d_ff_2_q), .Q(d_ff_4_q), .reset(in_2));  // open: Qn, preset, en
  LED led_5 (.in(d_ff_5_q));
  D_Flip_Flop #(.trigger("falling")) d_ff_5 (
    .clk(clock_1_out), .D(d_ff_3_q), .Q(d_ff_5_q), .reset(in_1));  // open: Qn, preset, en
  D_Flip_Flop #(.trigger("falling")) d_ff_6 (
    .clk(clock_2_out), .D(d_ff_4_q), .Q(d_ff_6_q), .reset(in_2));  // open: Qn, preset, en
  LED led_6 (.in(d_ff_6_q));
  LED led_7 (.in(d_ff_7_q));
  D_Flip_Flop #(.trigger("falling")) d_ff_7 (
    .clk(clock_1_out), .D(d_ff_5_q), .Q(d_ff_7_q), .reset(in_1));  // open: Qn, preset, en
  LED led_8 (.in(d_ff_8_q));
  D_Flip_Flop #(.trigger("falling")) d_ff_8 (
    .clk(clock_2_out), .D(d_ff_6_q), .Q(d_ff_8_q), .reset(in_2));  // open: Qn, preset, en
  LED led_9 (.in(d_ff_9_q));
  D_Flip_Flop #(.trigger("falling")) d_ff_9 (
    .clk(clock_1_out), .D(d_ff_7_q), .Q(d_ff_9_q), .reset(in_1));  // open: Qn, preset, en
  LED led_10 (.in(d_ff_10_q));
  D_Flip_Flop #(.trigger("falling")) d_ff_10 (
    .clk(clock_2_out), .D(d_ff_8_q), .Q(d_ff_10_q), .Qn(d_ff_10_qn), .reset(in_2));  // open: preset, en

  // Notes on the sheet:
  //   Ring counter
  //   Johnson's counter
endmodule
