// Logisim project S20210010027_Anushthan_Saxena_B1.circ as structural Verilog: 1 circuit, main circuit main
module main (
);

  wire and_1_out, and_2_out, and_3_out, and_4_out, and_5_out, and_6_out, and_7_out, clock_1_out, j_k_ff_1_q,
       j_k_ff_1_qn, j_k_ff_2_q, j_k_ff_2_qn, j_k_ff_3_q, j_k_ff_3_qn, j_k_ff_4_q, j_k_ff_4_qn, or_1_out,
       or_2_out, or_3_out;

  Clock clock_1 (.out(clock_1_out));
  and and_1 (and_1_out, j_k_ff_1_qn, j_k_ff_2_qn, j_k_ff_3_qn, j_k_ff_4_qn);
  and and_2 (and_2_out, j_k_ff_2_qn, j_k_ff_3_q, j_k_ff_4_q);
  J_K_Flip_Flop j_k_ff_1 (
    .J(and_1_out), .clk(clock_1_out), .K(and_2_out), .Q(j_k_ff_1_q), .Qn(j_k_ff_1_qn));  // open: preset, en, reset
  LED led_1 (.in(j_k_ff_1_q));
  and and_3 (and_3_out, j_k_ff_1_q, j_k_ff_4_q, j_k_ff_3_q);
  and and_4 (and_4_out, j_k_ff_1_qn, j_k_ff_2_q, j_k_ff_4_qn, j_k_ff_3_q);
  and and_5 (and_5_out, j_k_ff_1_q, j_k_ff_2_qn, j_k_ff_3_q);
  or or_1 (or_1_out, and_3_out, and_4_out);
  J_K_Flip_Flop j_k_ff_2 (
    .J(and_5_out), .clk(clock_1_out), .K(or_1_out), .Q(j_k_ff_2_q), .Qn(j_k_ff_2_qn));  // open: preset, en, reset
  LED led_2 (.in(j_k_ff_2_q));
  and and_6 (and_6_out, j_k_ff_1_qn, j_k_ff_2_qn, j_k_ff_4_q);
  LED led_3 (.in(j_k_ff_3_q));
  J_K_Flip_Flop j_k_ff_3 (
    .J(and_1_out), .clk(clock_1_out), .K(and_6_out), .Q(j_k_ff_3_q), .Qn(j_k_ff_3_qn));  // open: preset, en, reset
  or or_2 (or_2_out, and_4_out, and_5_out);
  or or_3 (or_3_out, and_5_out, and_7_out);
  and and_7 (and_7_out, j_k_ff_3_qn, j_k_ff_3_qn, j_k_ff_1_qn);
  LED led_4 (.in(j_k_ff_4_q));
  J_K_Flip_Flop j_k_ff_4 (
    .J(or_2_out), .clk(clock_1_out), .K(or_3_out), .Q(j_k_ff_4_q), .Qn(j_k_ff_4_qn));  // open: preset, en, reset

  // Notes on the sheet:
  //   A'
  //   A
  //   B'
  //   B
  //   D'
  //   C
  //   D
  //   C'
  //   A
  //   B
  //   C
  //   D
endmodule
