// Logisim project counter_down_sync.circ as structural Verilog: 1 circuit, main circuit main
module main (
);

  wire clock_1_out, d_ff_1_q, d_ff_1_qn, d_ff_2_q, d_ff_3_q, d_ff_4_q, or_1_out, or_2_out, xnor_1_out,
       xnor_2_out, xnor_3_out;

  Clock clock_1 (.out(clock_1_out));
  D_Flip_Flop d_ff_1 (.clk(clock_1_out), .D(d_ff_1_qn), .Q(d_ff_1_q), .Qn(d_ff_1_qn));  // open: preset, en, reset
  LED led_1 (.in(d_ff_1_q));
  xnor xnor_1 (xnor_1_out, d_ff_2_q, d_ff_1_q);
  D_Flip_Flop d_ff_2 (.clk(clock_1_out), .D(xnor_1_out), .Q(d_ff_2_q));  // open: Qn, preset, en, reset
  LED led_2 (.in(d_ff_2_q));
  or or_1 (or_1_out, d_ff_1_q, d_ff_2_q);
  xnor xnor_2 (xnor_2_out, or_1_out, d_ff_3_q);
  LED led_3 (.in(d_ff_3_q));
  D_Flip_Flop d_ff_3 (.clk(clock_1_out), .D(xnor_2_out), .Q(d_ff_3_q));  // open: Qn, preset, en, reset
  or or_2 (or_2_out, d_ff_1_q, d_ff_2_q, d_ff_3_q);
  LED led_4 (.in(d_ff_4_q));
  xnor xnor_3 (xnor_3_out, or_2_out, d_ff_4_q);
  D_Flip_Flop d_ff_4 (.clk(clock_1_out), .D(xnor_3_out), .Q(d_ff_4_q));  // open: Qn, preset, en, reset

  // Notes on the sheet:
  //   Q0
  //   Q1
  //   Synchronous 4 bit down counter
  //   Q2
  //   Q3
endmodule
