// Logisim project counter_up.circ as structural Verilog: 1 circuit, main circuit main
module main (
);

  wire and_1_out, and_2_out, clock_1_out, clock_2_out, d_ff_1_q, d_ff_1_qn, d_ff_2_q, d_ff_2_qn, d_ff_3_q,
       d_ff_3_qn, d_ff_4_q, d_ff_5_q, d_ff_5_qn, d_ff_6_q, d_ff_7_q, d_ff_7_qn, d_ff_8_q, xor_1_out,
       xor_2_out, xor_3_out;

  Clock clock_1 (.out(clock_1_out));
  Clock clock_2 (.out(clock_2_out));
  D_Flip_Flop d_ff_1 (.clk(clock_2_out), .D(d_ff_1_qn), .Q(d_ff_1_q), .Qn(d_ff_1_qn));  // open: preset, en, reset
  D_Flip_Flop d_ff_2 (.clk(clock_1_out), .D(d_ff_2_qn), .Q(d_ff_2_q), .Qn(d_ff_2_qn));  // open: preset, en, reset
  LED led (.in(d_ff_1_q));
  LED led_2 (.in(d_ff_2_q));
  xor xor_1 (xor_1_out, d_ff_4_q, d_ff_1_q);
  D_Flip_Flop d_ff_3 (.clk(d_ff_2_qn), .D(d_ff_3_qn), .Q(d_ff_3_q), .Qn(d_ff_3_qn));  // open: preset, en, reset
  D_Flip_Flop d_ff_4 (.clk(clock_2_out), .D(xor_1_out), .Q(d_ff_4_q));  // open: Qn, preset, en, reset
  LED led_3 (.in(d_ff_3_q));
  LED led_4 (.in(d_ff_4_q));
  and and_1 (and_1_out, d_ff_1_q, d_ff_4_q);
  D_Flip_Flop d_ff_5 (.clk(d_ff_3_qn), .D(d_ff_5_qn), .Q(d_ff_5_q), .Qn(d_ff_5_qn));  // open: preset, en, reset
  xor xor_2 (xor_2_out, and_1_out, d_ff_6_q);
  LED led_5 (.in(d_ff_5_q));
  LED led_6 (.in(d_ff_6_q));
  D_Flip_Flop d_ff_6 (.clk(clock_2_out), .D(xor_2_out), .Q(d_ff_6_q));  // open: Qn, preset, en, reset
  and and_2 (and_2_out, d_ff_1_q, d_ff_4_q, d_ff_6_q);
  LED led_7 (.in(d_ff_7_q));
  D_Flip_Flop d_ff_7 (.clk(d_ff_5_qn), .D(d_ff_7_qn), .Q(d_ff_7_q), .Qn(d_ff_7_qn));  // open: preset, en, reset
  LED led_8 (.in(d_ff_8_q));
  xor xor_3 (xor_3_out, and_2_out, d_ff_8_q);
  D_Flip_Flop d_ff_8 (.clk(clock_2_out), .D(xor_3_out), .Q(d_ff_8_q));  // open: Qn, preset, en, reset

  // Notes on the sheet:
  //   Q0
  //   Q0
  //   Asynchronous 4 bit up counter
  //   Q1
  //   Q1
  //   synchronous 4 bit up counter
  //   Q2
  //   Q2
  //   Q3
  //   Q3
endmodule
