// Logisim project latches.circ as structural Verilog: 1 circuit, main circuit main
module main (
  input  R,
  input  S,
  input  R_2,
  input  En,
  input  S_2,
  input  En_2,
  input  D,
  output out_8,
  output out_9,
  output out_10,
  output out_11,
  output out_12,
  output out_13
);

  wire and_1_out, and_2_out, and_3_out, and_4_out, not_1_out;

  not not_1 (not_1_out, D);
  and and_1 (and_1_out, R_2, En);
  and and_2 (and_2_out, not_1_out, En_2);
  nor nor_1 (out_8, R, out_9);
  nor nor_2 (out_9, out_8, S);
  and and_3 (and_3_out, En, S_2);
  and and_4 (and_4_out, En_2, D);
  nor nor_3 (out_10, and_1_out, out_11);
  nor nor_4 (out_11, out_10, and_3_out);
  nor nor_5 (out_12, and_2_out, out_13);
  nor nor_6 (out_13, out_12, and_4_out);

  // Notes on the sheet:
  //   SR Latch
  //   Gated SR Latch
  //   D Latch
endmodule
